// Logisim project alarme_industrial.circ as structural Verilog: 1 circuit, main circuit main
module main (
  input  A,
  input  B,
  input  C
);

  wire and_1_out, or_1_out;

  or or_1 (or_1_out, A, B);
  LED led_1 (.in(and_1_out));
  and and_1 (and_1_out, or_1_out, C);
endmodule
